# Fritzing sketch IoTWorkshop_Blink (saved by Fritzing 0.9.3b)
breadboards: 1

parts:
  U1 = NodeMCU V1.0
  R8 = Resistor [tolerance=±5% resistance=10k package=THT]
  LED1 = LED - 5mm [color="Red (633nm)" package="5 mm [THT]"]

nets:
  N1: U1.GND, LED1.cathode
  N2: U1.D5, R8.Pin_1
  N3: R8.Pin_0, LED1.anode

notes:
  In this example, potentiometer values are read in through an 'Analog In' pin A0.
  The values are then used to activate an LED.
  Download the Arduino Sketch here:
  https://github.com/seattle-diy-iot/iot-workshop-Fading

custom parts:
  NodeMCU V1.0: ESP8266 based NodeMCU
